# Fritzing sketch power_metter_ina219 (saved by Fritzing 0.9.1b)
breadboards: 1

parts:
  INA1 = INA219 DC Current Sensor Breakout
  Part1 = Arduino Pro Mini v13
  VCC1 = Battery
  JP1 = screwterminal 5mm [package=screwterminal-5mm-2pin]

nets:
  VCC: INA1.VCC, Part1.VCC
  GND: INA1.GND, Part1.GND, VCC1.-, JP1.1
  N1: INA1.SCL, Part1.A5
  N2: INA1.SDA, Part1.A4
  N3: INA1.Vin-2, JP1.2
  N4: INA1.Vin+2, VCC1.+

notes:
  Power source
  Power supply for circuit

custom parts:
  INA219 DC Current Sensor Breakout: INA DC Current Sensor Breakout
  screwterminal 5mm: Header 2 Standard 2-pin 0.1 header. Use with straight break away headers (SKU : PRT-08432). ebay 2 Pin Screw Terminal Block Connector 5.0mm Pitch KF-301-2P .
